# Fritzing sketch LDRStepperUno9V (saved by Fritzing 0.9.2b)
breadboards: 1

parts:
  Part1 = Arduino Uno (Rev3) - ICSP
  M2 = Stepper Motor - Bipolar
  Part2 = EasyDriver_v44
  LDR1 = Photocell (LDR) [package=THT]
  part = Resistor [tolerance=±5% resistance=10k package=THT]
  part_2 = Battery block 9V

nets:
  N1: Part1.A0, LDR1.pin_1, part.Pin_0
  5V: Part1.5V, Part2.VCC, part.Pin_1
  N2: Part1.D2, Part2.STEP
  N3: Part1.D3_PWM, Part2.DIR
  N4: Part1.D4, Part2.MS1
  N5: Part1.D5_PWM, Part2.MS2
  N6: Part1.D6_PWM, Part2.ENABLE
  GND: Part1.GND, Part2.GND, LDR1.pin_0, part_2.-
  N7: Part1.VIN, Part2.V+, part_2.+
  N8: M2.A, Part2.OUT2A
  N9: M2.C, Part2.OUT2B
  N10: M2.B, Part2.OUT1A
  N11: M2.D, Part2.OUT1B
